# Fritzing sketch fritzing (saved by Fritzing 0.9.3b)
breadboards: 1

parts:
  Componente1 = Arduino Uno (Rev3)
  M1 = DC Motor
  M2 = DC Motor
  IC1 = L293D [package=THT]
  VCC1 = Battery block 9V  # not connected

nets:
  N1: Componente1.D9_PWM, IC1.In_1
  N2: Componente1.D10_PWM/SS, IC1.In_2
  N3: Componente1.GND, IC1.0V
  N4: Componente1.D5_PWM, IC1.In_4
  N5: Componente1.D6_PWM, IC1.In_3
  N6: Componente1.5V, IC1.Enable_1, IC1.Enable_2, IC1.+V
  N7: Componente1.VIN, IC1.+Vmotor
  N8: M1.pin_1, IC1.Out_4_(_Controlled_by_Enable_2_)
  N9: M1.pin_2, IC1.Out_3_(_Controlled_by_Enable_2_)
  N10: M2.pin_1, IC1.Out_2_(_Controlled_by_Enable_1_)
  N11: M2.pin_2, IC1.Out_1_(_Controlled_by_Enable_1_)
